# Fritzing sketch Arbol de navidad (saved by Fritzing 0.9.3b)
breadboards: 2

parts:
  Componente1 = Arduino Uno (Rev3) - ICSP
  J1 = Piezo Speaker
  U1 = 74HC595 [package="DIP16 [THT]"]
  U2 = 74HC595 [package="DIP16 [THT]"]
  R1 = Resistor [tolerance=±5% resistance=220 package="2010 [SMD]"]
  R2 = Resistor [tolerance=±5% resistance=220 package="2010 [SMD]"]
  R3 = Resistor [tolerance=±5% resistance=220 package="2010 [SMD]"]
  R4 = Resistor [tolerance=±5% resistance=220 package="2010 [SMD]"]
  R5 = Resistor [tolerance=±5% resistance=220 package="2010 [SMD]"]
  R6 = Resistor [tolerance=±5% resistance=220 package="2010 [SMD]"]
  R7 = Resistor [tolerance=±5% resistance=220 package="2010 [SMD]"]
  R8 = Resistor [tolerance=±5% resistance=220 package="2010 [SMD]"]
  R9 = Resistor [tolerance=±5% resistance=220 package="2010 [SMD]"]
  R10 = Resistor [tolerance=±5% resistance=220 package="2010 [SMD]"]
  R11 = Resistor [tolerance=±5% resistance=220 package="2010 [SMD]"]
  R12 = Resistor [tolerance=±5% resistance=220 package="2010 [SMD]"]
  R13 = Resistor [tolerance=±5% resistance=220 package="2010 [SMD]"]
  R14 = Resistor [tolerance=±5% resistance=220 package="2010 [SMD]"]
  R15 = Resistor [tolerance=±5% resistance=220 package="2010 [SMD]"]
  R16 = Resistor [tolerance=±5% resistance=220 package="2010 [SMD]"]
  LED2 = LED - 3mm [color="Red (633nm)" package="3 mm [THT]"]
  LED1 = LED - 3mm [color="Red (633nm)" package="3 mm [THT]"]
  LED3 = LED - 3mm [color="Red (633nm)" package="3 mm [THT]"]
  LED4 = LED - 3mm [color="Red (633nm)" package="3 mm [THT]"]
  LED5 = LED - 3mm [color="Red (633nm)" package="3 mm [THT]"]
  LED6 = LED - 3mm [color="Red (633nm)" package="3 mm [THT]"]
  LED7 = LED - 3mm [color="Red (633nm)" package="3 mm [THT]"]
  LED8 = LED - 3mm [color="Red (633nm)" package="3 mm [THT]"]
  LED9 = LED - 3mm [color="Red (633nm)" package="3 mm [THT]"]
  LED10 = LED - 3mm [color="Red (633nm)" package="3 mm [THT]"]
  LED11 = LED - 3mm [color="Red (633nm)" package="3 mm [THT]"]
  LED12 = LED - 3mm [color="Red (633nm)" package="3 mm [THT]"]
  LED13 = LED - 3mm [color="Red (633nm)" package="3 mm [THT]"]
  LED14 = LED - 3mm [color="Red (633nm)" package="3 mm [THT]"]
  LED15 = LED - 3mm [color="Red (633nm)" package="3 mm [THT]"]
  LED16 = LED - 3mm [color="Red (633nm)" package="3 mm [THT]"]

nets:
  VCC: Componente1.5V, U1.MR, U1.VCC, U2.MR, U2.VCC
  GND: Componente1.GND, J1.pin1, U1.GND, U1.OE, U2.GND, U2.OE, LED2.cathode, LED1.cathode, LED3.cathode, LED4.cathode, LED5.cathode, LED6.cathode, LED7.cathode, LED8.cathode, LED9.cathode, LED10.cathode, LED11.cathode, LED12.cathode, LED13.cathode, LED14.cathode, LED15.cathode, LED16.cathode
  N1: Componente1.D11_PWM/MOSI, J1.pin2
  N2: Componente1.D2, U1.ST_CP, U2.ST_CP
  N3: Componente1.D3_PWM, U2.DS
  N4: Componente1.D5_PWM, U1.SH_CP, U2.SH_CP
  N5: U1.Q1, R10.Pin_0
  N6: U1.Q2, R13.Pin_0
  N7: U1.Q3, R16.Pin_0
  N8: U1.Q4, R15.Pin_0
  N9: U1.Q5, R11.Pin_0
  N10: U1.Q6, R14.Pin_0
  N11: U1.Q7, R12.Pin_0
  N12: U1.DS, U2.Q7'
  N13: U1.Q0, R9.Pin_0
  N14: U2.Q1, R2.Pin_0
  N15: U2.Q2, R3.Pin_0
  N16: U2.Q3, R4.Pin_0
  N17: U2.Q4, R5.Pin_0
  N18: U2.Q5, R6.Pin_0
  N19: U2.Q6, R7.Pin_0
  N20: U2.Q7, R8.Pin_0
  N21: U2.Q0, R1.Pin_0
  N22: R1.Pin_1, LED1.anode
  N23: R2.Pin_1, LED2.anode
  N24: R3.Pin_1, LED4.anode
  N25: R4.Pin_1, LED3.anode
  N26: R5.Pin_1, LED6.anode
  N27: R6.Pin_1, LED7.anode
  N28: R7.Pin_1, LED5.anode
  N29: R8.Pin_1, LED8.anode
  N30: R9.Pin_1, LED12.anode
  N31: R10.Pin_1, LED14.anode
  N32: R11.Pin_1, LED15.anode
  N33: R12.Pin_1, LED9.anode
  N34: R13.Pin_1, LED11.anode
  N35: R14.Pin_1, LED16.anode
  N36: R15.Pin_1, LED10.anode
  N37: R16.Pin_1, LED13.anode
